// Logisim project 2115HW4.circ as structural Verilog
module register_file (
  input  [2:0] Read_Register_1,
  input  Write,
  input  [2:0] Read_Register_2,
  input  [2:0] Write_Rigister,
  input  [15:0] Write_Data,
  input  [15:0] Read_ra,
  input  Write_ra,
  input  Clock,
  input  Reset,
  output [15:0] Read_Data_1,
  output [15:0] Read_Data_2
);

  wire and_1_out, and_2_out, and_3_out, and_4_out, and_5_out, and_6_out, and_7_out, and_8_out, and_9_out,
       decoder_1_out0, decoder_1_out1, decoder_1_out2, decoder_1_out3, decoder_1_out4, decoder_1_out5,
       decoder_1_out6, decoder_1_out7;
  wire [15:0] r1_q, r2_q, r3_q, r4_q, r5_q, r6_q, r7_q, r8_q;

  Decoder #(.select(3)) decoder_1 (
    .out0(decoder_1_out0), .out1(decoder_1_out1), .out2(decoder_1_out2), .out3(decoder_1_out3),
    .out4(decoder_1_out4), .out5(decoder_1_out5), .out6(decoder_1_out6), .out7(decoder_1_out7),
    .sel(Write_Rigister), .en(1'b1));
  and and_1 (and_1_out, decoder_1_out0, Write);
  and and_2 (and_2_out, decoder_1_out1, Write);
  and and_3 (and_3_out, decoder_1_out2, Write);
  and and_4 (and_4_out, decoder_1_out3, Write);
  and and_5 (and_5_out, decoder_1_out4, Write);
  and and_6 (and_6_out, decoder_1_out5, Write);
  and and_7 (and_7_out, decoder_1_out6, Write);
  and and_8 (and_8_out, decoder_1_out7, Write);
  and and_9 (and_9_out, Write, Write_ra);
  Register #(.width(16)) r1 (.D(Write_Data), .en(and_1_out), .Q(r1_q), .clk(Clock), .clr(Reset));
  Register #(.width(16)) r2 (.D(Write_Data), .en(and_2_out), .Q(r2_q), .clk(Clock), .clr(Reset));
  Register #(.width(16)) r3 (.D(Write_Data), .en(and_3_out), .Q(r3_q), .clk(Clock), .clr(Reset));
  Register #(.width(16)) r4 (.D(Write_Data), .en(and_4_out), .Q(r4_q), .clk(Clock), .clr(Reset));
  Register #(.width(16)) r5 (.D(Write_Data), .en(and_5_out), .Q(r5_q), .clk(Clock), .clr(Reset));
  Register #(.width(16)) r6 (.D(Write_Data), .en(and_6_out), .Q(r6_q), .clk(Clock), .clr(Reset));
  Register #(.width(16)) r7 (.D(Write_Data), .en(and_7_out), .Q(r7_q), .clk(Clock), .clr(Reset));
  Register #(.width(16)) r8 (.D(Write_Data), .en(and_8_out), .Q(r8_q), .clk(Clock), .clr(Reset));
  Register #(.width(16)) ra (.D(Write_Data), .en(and_9_out), .Q(Read_ra), .clk(Clock), .clr(Reset));
  Multiplexer #(.select(3), .width(16)) multiplexer_1 (
    .in0(r1_q), .in1(r2_q), .in2(r3_q), .in3(r4_q), .in4(r5_q), .in5(r6_q), .in6(r7_q), .in7(r8_q),
    .out(Read_Data_1), .sel(Read_Register_1));  // open: en
  Multiplexer #(.select(3), .width(16)) multiplexer_2 (
    .in0(r1_q), .in1(r2_q), .in2(r3_q), .in3(r4_q), .in4(r5_q), .in5(r6_q), .in6(r7_q), .in7(r8_q),
    .out(Read_Data_2), .sel(Read_Register_2));  // open: en
endmodule

module Control_Unit (
  input  op0,
  input  op1,
  input  op2,
  input  op3,
  input  op4,
  output RegDst,
  output RegWrite,
  output ALUSrc,
  output Branch,
  output MemRead,
  output MemWrite,
  output MemtoReg,
  output Li,
  output Write_ra,
  output Read_ra,
  output EnReboot
);

  wire and_1_out, and_2_out, and_3_out, and_4_out, and_5_out, and_6_out, and_7_out, and_8_out, and_9_out,
       and_10_out, and_11_out, and_12_out, and_13_out, and_14_out, and_15_out, not_1_out, not_2_out,
       not_3_out, not_4_out, not_5_out, not_6_out, not_7_out, not_8_out, not_9_out, not_10_out, not_11_out,
       not_12_out, not_13_out, not_14_out, not_15_out, not_16_out, not_17_out, not_18_out, not_19_out,
       not_20_out, not_21_out, not_22_out, not_23_out, not_24_out, not_25_out, not_26_out, not_27_out,
       not_28_out, not_29_out, not_30_out, not_31_out, not_32_out, not_33_out, not_34_out, not_35_out,
       not_36_out, not_37_out, not_38_out, not_39_out, not_40_out, not_41_out;

  not not_1 (not_1_out, op0);
  not not_2 (not_2_out, op1);
  not not_3 (not_3_out, op2);
  not not_4 (not_4_out, op0);
  not not_5 (not_5_out, op1);
  not not_6 (not_6_out, op2);
  not not_7 (not_7_out, op3);
  not not_8 (not_8_out, op4);
  not not_9 (not_9_out, op0);
  not not_10 (not_10_out, op1);
  not not_11 (not_11_out, op2);
  not not_12 (not_12_out, op0);
  not not_13 (not_13_out, op3);
  not not_14 (not_14_out, op3);
  not not_15 (not_15_out, op4);
  not not_16 (not_16_out, op0);
  not not_17 (not_17_out, op1);
  not not_18 (not_18_out, op4);
  not not_19 (not_19_out, op1);
  not not_20 (not_20_out, op3);
  not not_21 (not_21_out, op4);
  not not_22 (not_22_out, op1);
  not not_23 (not_23_out, op2);
  not not_24 (not_24_out, op3);
  not not_25 (not_25_out, op2);
  not not_26 (not_26_out, op4);
  not not_27 (not_27_out, op4);
  not not_28 (not_28_out, op2);
  not not_29 (not_29_out, op1);
  not not_30 (not_30_out, op3);
  not not_31 (not_31_out, op1);
  not not_32 (not_32_out, op4);
  not not_33 (not_33_out, op1);
  not not_34 (not_34_out, op3);
  not not_35 (not_35_out, op0);
  not not_36 (not_36_out, op3);
  not not_37 (not_37_out, op4);
  not not_38 (not_38_out, op3);
  not not_39 (not_39_out, op4);
  not not_40 (not_40_out, op3);
  not not_41 (not_41_out, op4);
  and and_1 (and_1_out, not_1_out, not_2_out, not_3_out, op4);
  and and_2 (and_2_out, not_4_out, not_5_out, not_6_out, op3);
  and and_3 (and_3_out, op1, op2, not_7_out);
  and and_4 (and_4_out, op1, op2, not_8_out);
  and and_5 (and_5_out, not_9_out, not_10_out, not_11_out);
  and and_6 (and_6_out, not_12_out, not_13_out);
  and and_7 (and_7_out, not_14_out, not_15_out);
  and and_8 (and_8_out, not_16_out, not_17_out, op4);
  and and_9 (and_9_out, op1, not_18_out);
  and and_10 (and_10_out, not_19_out, not_20_out, not_21_out);
  and and_11 (and_11_out, not_22_out, op2);
  and and_12 (and_12_out, op2, op3, op4);
  and and_13 (and_13_out, op1, not_23_out, not_24_out);
  and and_14 (and_14_out, op1, not_25_out, not_26_out);
  and and_15 (and_15_out, op0, not_27_out);
  and and_16 (Branch, op1, not_28_out, op3, op4);
  and and_17 (MemRead, not_29_out, op2, not_30_out, op4);
  and and_18 (MemWrite, not_31_out, op2, op3, not_32_out);
  and and_19 (MemtoReg, not_33_out, op2, not_34_out, op4);
  or or_1 (Li, not_35_out, not_36_out, not_37_out);
  and and_20 (Write_ra, op0, not_38_out, not_39_out);
  and and_21 (Read_ra, op0, not_40_out, op4);
  and and_22 (EnReboot, op0, op3, not_41_out);
  or or_2 (RegDst, and_1_out, and_2_out, and_3_out, and_4_out);
  or or_3 (RegWrite, and_5_out, and_6_out, and_7_out, and_8_out, and_9_out);
  or or_4 (ALUSrc, and_10_out, and_11_out, and_12_out, and_13_out, and_14_out, and_15_out);
endmodule

module ALU (
  input  [15:0] ReadData1,
  input  [15:0] ReadData2,
  input  [3:0] ALUControl,
  output [15:0] out_4
);

  wire comparator_1_eq, comparator_1_lt, or_2_out;
  wire [3:0] bit_extender_1_out, bit_extender_2_out;
  wire [15:0] adder_1_out, adder_2_out, and_1_out, bit_extender_3_out, bit_extender_4_out, or_1_out,
       shifter_1_out, shifter_2_out, subtractor_1_out;

  Comparator #(.width(16)) comparator_1 (
    .a(ReadData1), .b(ReadData2), .eq(comparator_1_eq), .lt(comparator_1_lt));  // open: gt
  Bit_Extender #(.in_width(16), .out_width(4), .\type ("sign")) bit_extender_1 (
    .in(ReadData2), .out(bit_extender_1_out));
  Bit_Extender #(.in_width(16), .out_width(4), .\type ("sign")) bit_extender_2 (
    .in(ReadData2), .out(bit_extender_2_out));
  Adder #(.width(16)) adder_1 (.a({16{1'b0}}), .b(ReadData2), .out(adder_1_out));  // open: cin, cout
  Adder #(.width(16)) adder_2 (.a(ReadData1), .b(ReadData2), .out(adder_2_out));  // open: cin, cout
  assign and_1_out = ReadData1 & ReadData2;  // AND_Gate and_1, 16 bits wide
  assign or_1_out = ReadData1 | ReadData2;  // OR_Gate or_1, 16 bits wide
  Subtractor #(.width(16)) subtractor_1 (.a({16{1'b0}}), .b(ReadData2), .out(subtractor_1_out));  // open: bin, bout
  or or_2 (or_2_out, comparator_1_eq, comparator_1_lt);
  Shifter #(.width(16)) shifter_1 (.in(ReadData1), .\dist (bit_extender_1_out), .out(shifter_1_out));
  Shifter #(.width(16), .shift("lr")) shifter_2 (.in(ReadData1), .\dist (bit_extender_2_out), .out(shifter_2_out));
  assign bit_extender_3_out = {{15{1'b0}}, or_2_out};  // Bit_Extender bit_extender_3
  assign bit_extender_4_out = {{15{1'b0}}, comparator_1_lt};  // Bit_Extender bit_extender_4
  Multiplexer #(.select(4), .width(16)) multiplexer_1 (
    .in0(adder_1_out), .in1(adder_2_out), .in2(and_1_out), .in3(or_1_out), .in4(subtractor_1_out),
    .in5(bit_extender_3_out), .in6(bit_extender_4_out), .in7(shifter_1_out), .in8(shifter_2_out),
    .out(out_4), .sel(ALUControl), .en(1'b1));  // open: in9, in10, in11, in12, in13, in14, in15
endmodule

module ALUControl (
  input  op0,
  input  op1,
  input  op2,
  input  op3,
  input  op4,
  output ALUop0,
  output ALUop1,
  output ALUop2,
  output ALUop3
);

  wire and_2_out, and_3_out, and_4_out, and_5_out, and_6_out, and_7_out, and_8_out, and_9_out, and_10_out,
       and_11_out, not_1_out, not_2_out, not_3_out, not_4_out, not_5_out, not_6_out, not_7_out, not_8_out,
       not_9_out, not_10_out, not_11_out, not_12_out, not_13_out, not_14_out, not_15_out;

  and and_1 (ALUop0, op1, op2, op4);
  not not_1 (not_1_out, op3);
  not not_2 (not_2_out, op4);
  not not_3 (not_3_out, op1);
  not not_4 (not_4_out, op2);
  not not_5 (not_5_out, op2);
  not not_6 (not_6_out, op3);
  not not_7 (not_7_out, op3);
  not not_8 (not_8_out, op4);
  not not_9 (not_9_out, op2);
  not not_10 (not_10_out, op1);
  not not_11 (not_11_out, op2);
  not not_12 (not_12_out, op2);
  not not_13 (not_13_out, op3);
  not not_14 (not_14_out, op4);
  not not_15 (not_15_out, op4);
  and and_2 (and_2_out, op2, not_1_out, not_2_out);
  and and_3 (and_3_out, op1, op3);
  and and_4 (and_4_out, not_3_out, not_4_out, op3);
  and and_5 (and_5_out, op1, not_5_out, not_6_out);
  and and_6 (and_6_out, op1, not_7_out, not_8_out);
  and and_7 (and_7_out, op1, not_9_out, op4);
  and and_8 (and_8_out, not_10_out, not_11_out, op4);
  and and_9 (and_9_out, not_12_out, not_13_out, op4);
  and and_10 (and_10_out, op1, op3, not_14_out);
  and and_11 (and_11_out, op1, op2, not_15_out);
  or or_1 (ALUop1, and_2_out, and_3_out);
  or or_2 (ALUop2, and_4_out, and_5_out, and_6_out, and_7_out);
  or or_3 (ALUop3, and_8_out, and_9_out, and_10_out, and_11_out);
endmodule
